// Logisim project utility.circ as structural Verilog: 2 circuits, main circuit Increment (4 bits)
module Increment__4_bits (
  input  [3:0] in_1,
  output [3:0] out_2
);

  Adder #(.width(4)) adder_1 (.a(in_1), .b(4'b0001), .out(out_2));  // open: cin, cout
endmodule

module Not_Zero__6_bits (
  input  [5:0] in_1,
  output out_2
);

  wire or_1_out;

  or or_1 (or_1_out, in_1[0], in_1[1], in_1[2], in_1[3], in_1[4], in_1[5]);
  Transistor #(.\type ("n")) transistor_1 (.in(1'b0), .out(out_2), .gate(or_1_out));
endmodule
