// Logisim project main.circ as structural Verilog: 1 circuit, main circuit Game
module Game (
);

  wire and_1_out, Awaiting_user, button_1_out, button_2_out, button_3_out, button_4_out, button_5_out,
       button_6_out, button_driver_1_trigger, button_register_2_clock_2, button_register_2_r___w_selector_2,
       button_register_2_zero, button_register_3_clock_2, button_register_3_r___w_selector_2,
       button_register_3_zero, button_register_4_clock_2, button_register_4_r___w_selector_2,
       button_register_5_clock_2, button_register_5_r___w_selector_2, button_register_6_clock_2,
       button_register_6_r___w_selector_2, button_register_7_clock_2, button_register_7_r___w_selector_2,
       button_register_8_clock_2, button_register_8_r___w_selector_2, button_register_9_clock_2,
       button_register_9_r___w_selector_2, button_register_10_clock_2, button_register_10_r___w_selector_2,
       button_register_11_clock_2, button_register_11_r___w_selector_2, button_register_12_clock_2,
       button_register_12_r___w_selector_2, button_register_13_clock_2, button_register_13_r___w_selector_2,
       button_register_14_clock_2, button_register_14_r___w_selector_2, C, Calculating_machine,
       Calculating_user, Checking_rules, Clock, Computer, Data, Data_Type, decoder_1_out0, decoder_1_out1,
       decoder_2_out0, decoder_2_out1, Game_starts, Gamepad, H, Initialization, Instructions, L,
       Machine_thinks, MD, Memory, memory_manager_1_c, memory_manager_1_d, not_1_out, not_2_out, R, R___W,
       ram_address_manager_1_is_selected, Referee, User, W_out;
  wire [3:0] Button, button_driver_1_address_2, button_driver_2_address_2, button_driver_3_address_2,
       button_driver_4_address_2, button_driver_5_address_2, button_driver_6_address_2,
       button_register_1_tens, button_register_1_units, button_register_2_address_2,
       button_register_2_driver, button_register_2_position___1, button_register_2_tens,
       button_register_2_units, button_register_3_address_2, button_register_3_position___1,
       button_register_3_tens, button_register_3_units, button_register_4_address_2,
       button_register_4_driver, button_register_4_position___1, button_register_4_tens,
       button_register_4_units, button_register_5_address_2, button_register_5_position___1,
       button_register_5_tens, button_register_5_units, button_register_6_address_2,
       button_register_6_driver, button_register_6_position___1, button_register_6_tens,
       button_register_6_units, button_register_7_address_2, button_register_7_position___1,
       button_register_7_tens, button_register_7_units, button_register_8_address_2,
       button_register_8_driver, button_register_8_position___1, button_register_8_tens,
       button_register_8_units, button_register_9_address_2, button_register_9_position___1,
       button_register_9_tens, button_register_9_units, button_register_10_address_2,
       button_register_10_driver, button_register_10_position___1, button_register_10_tens,
       button_register_10_units, button_register_11_address_2, button_register_11_position___1,
       button_register_11_tens, button_register_11_units, button_register_12_address_2,
       button_register_12_driver, button_register_12_position___1, button_register_12_tens,
       button_register_12_units, button_register_13_address_2, button_register_13_position___1,
       button_register_13_tens, button_register_13_units, button_register_14_address_2,
       button_register_14_position___1, button_register_14_tens, button_register_14_units,
       gamepad_address_manager_1_gamepad_address, increment_4_bits_1_out_2, ram_address_manager_1_ram_address;
  wire [7:0] Address_Bus, button_register_2_dataout, button_register_3_dataout, button_register_4_dataout,
       button_register_5_dataout, button_register_6_dataout, button_register_7_dataout,
       button_register_8_dataout, button_register_9_dataout, button_register_10_dataout,
       button_register_11_dataout, button_register_12_dataout, button_register_13_dataout,
       button_register_14_dataout, cdm_8_mark5_1_p13, cdm_8_mark5_1_p14, Data_Bus, G_In, G_Out, PC, PS, r1,
       r2, r3, r4, SP;

  // CdM_8_mark5 cdm_8_mark5_1: pin names not known; wires that end beside it: r1, r2, Clock, r3, r4, PC, SP, PS, Data_Type, Memory, R___W, Address_Bus, cdm_8_mark5_1_p13, cdm_8_mark5_1_p14
  RAM_Address_Manager ram_address_manager_1 (
    .Input_Address(Address_Bus), .RAM_Address(ram_address_manager_1_ram_address),
    .Is_Selected(ram_address_manager_1_is_selected), .Data(Data));
  assign Data_Bus = decoder_1_out0 ? cdm_8_mark5_1_p13 : 8'bz;  // Controlled_Buffer controlled_buffer_1
  Decoder #(.disabled(0), .enable("false")) decoder_1 (.out0(decoder_1_out0), .out1(decoder_1_out1), .sel(R___W));
  assign cdm_8_mark5_1_p14 = decoder_1_out1 ? Data_Bus : 8'bz;  // Controlled_Buffer controlled_buffer_2
  ROM rom_1 (.addr(Address_Bus), .data(Data_Bus), .sel(Initialization));
  Clock clock_1 (.out(Clock));
  assign G_In = decoder_2_out0 ? Data_Bus : 8'bz;  // Controlled_Buffer controlled_buffer_3
  Decoder #(.disabled(0)) decoder_2 (.out0(decoder_2_out0), .out1(decoder_2_out1), .sel(R___W), .en(Gamepad));
  assign Data_Bus = decoder_2_out1 ? G_Out : 8'bz;  // Controlled_Buffer controlled_buffer_4
  RAM #(.addrWidth(4)) ram_1 (
    .addr(ram_address_manager_1_ram_address), .data(Data_Bus), .sel(ram_address_manager_1_is_selected),
    .clk(Clock), .ld(R___W));  // open: clr
  Decoder #(.disabled(0)) decoder_3 (.out0(Instructions), .out1(Data), .sel(Data_Type), .en(Memory));
  ROM rom_2 (.addr(Address_Bus), .data(Data_Bus), .sel(Referee));
  Memory_Manager memory_manager_1 (
    .Data(Data_Bus), .Data_2(Data), .Address(Address_Bus), .Control_Byte(8'hf0), .Clock(Clock),
    .A(Game_starts), .B(Checking_rules), .C(memory_manager_1_c), .D(memory_manager_1_d));
  assign Awaiting_user = MD ? memory_manager_1_c : 1'bz;  // Controlled_Buffer controlled_buffer_5
  assign Machine_thinks = MD ? memory_manager_1_d : 1'bz;  // Controlled_Buffer controlled_buffer_6
  ROM rom_3 (.addr(Address_Bus), .data(Data_Bus), .sel(User));
  User_Input_Register user_input_register_1 (
    .Program_Input(Data_Bus), .Address(Address_Bus), .Data(Data), .Output(Data_Bus), .R___W(R___W),
    .Is_Active(MD), .User_Input(Button));
  and and_1 (and_1_out, Memory, Instructions);
  Big_Controlled_Buffer big_controlled_buffer_1 (
    .A(Game_starts), .B(Checking_rules), .C(memory_manager_1_c), .D(memory_manager_1_d),
    .A_2(Initialization), .B_2(Referee), .\С (User), .D_2(Computer), .Control(and_1_out));
  assign Calculating_user = not_1_out ? memory_manager_1_c : 1'bz;  // Controlled_Buffer controlled_buffer_7
  assign Calculating_machine = not_1_out ? memory_manager_1_d : 1'bz;  // Controlled_Buffer controlled_buffer_8
  not not_1 (not_1_out, MD);
  ROM rom_4 (.addr(Address_Bus), .data(Data_Bus), .sel(Computer));
  // Computer_Node computer_node_1: pin names not known
  LED led_1 (.in(C));
  LED led_2 (.in(C));
  Pull_Resistor pull_resistor_1 (.node(C));
  LED led_3 (.in(C));
  Hex_Digit_Display hex_digit_display_1 (.value(button_register_1_tens));  // open: dp
  Gamepad_Address_Manager gamepad_address_manager_1 (
    .Input_Address(Address_Bus), .Data(Data), .Gamepad_Address(gamepad_address_manager_1_gamepad_address),
    .Is_Selected(Gamepad));
  Button_Register button_register_1 (
    .Data(button_register_3_dataout), .Position(button_register_3_position___1),
    .Address(button_register_3_address_2), .Clock(button_register_3_clock_2),
    .R___W_Selector(button_register_3_r___w_selector_2), .Dataout(G_Out), .Tens(button_register_1_tens),
    .Units(button_register_1_units));  // open: Position___1, Address_2, Driver, Clock_2, R___W_Selector_2, Zero
  Hex_Digit_Display hex_digit_display_2 (.value(button_register_1_units));  // open: dp
  nand W (W_out, Data, ~R___W, Gamepad);  // NAND_Gate
  Hex_Digit_Display hex_digit_display_3 (.value(button_register_3_tens));  // open: dp
  Win_Lose_Draw win_lose_draw_1 (
    .Tens(button_register_1_tens), .Units(button_register_1_units), .Is_Zero(button_register_3_zero),
    .Another(R), .out_5(C), .out_6(L));
  Hex_Digit_Display hex_digit_display_4 (.value(button_register_2_tens));  // open: dp
  Button_Register button_register_2 (
    .Data(G_In), .Position(4'b0000), .Address(gamepad_address_manager_1_gamepad_address), .Clock(Clock),
    .R___W_Selector(W_out), .Dataout(button_register_2_dataout),
    .Position___1(button_register_2_position___1), .Address_2(button_register_2_address_2),
    .Driver(button_register_2_driver), .Clock_2(button_register_2_clock_2),
    .R___W_Selector_2(button_register_2_r___w_selector_2), .Zero(button_register_2_zero),
    .Tens(button_register_2_tens), .Units(button_register_2_units));
  Button_Driver button_driver_1 (
    .Position(button_register_2_driver), .Address_2(button_driver_1_address_2),
    .Address(button_driver_2_address_2), .Button(button_1_out), .Trigger(button_driver_1_trigger));
  assign Button = not_2_out ? button_driver_1_address_2 : 4'bz;  // Controlled_Buffer controlled_buffer_9
  not not_2 (not_2_out, button_driver_1_trigger);
  // Computer_Node computer_node_2: pin names not known
  Button_Register button_register_3 (
    .Data(button_register_5_dataout), .Position(button_register_5_position___1),
    .Address(button_register_5_address_2), .Clock(button_register_5_clock_2),
    .R___W_Selector(button_register_5_r___w_selector_2), .Dataout(button_register_3_dataout),
    .Position___1(button_register_3_position___1), .Address_2(button_register_3_address_2),
    .Clock_2(button_register_3_clock_2), .R___W_Selector_2(button_register_3_r___w_selector_2),
    .Zero(button_register_3_zero), .Tens(button_register_3_tens), .Units(button_register_3_units));  // open: Driver
  Hex_Digit_Display hex_digit_display_5 (.value(button_register_3_units));  // open: dp
  LED led_4 (.in(Calculating_machine));
  LED led_5 (.in(Calculating_machine));
  LED led_6 (.in(Calculating_machine));
  Hex_Digit_Display hex_digit_display_6 (.value(button_register_2_units));  // open: dp
  Button_Register button_register_4 (
    .Data(button_register_2_dataout), .Position(button_register_2_position___1),
    .Address(button_register_2_address_2), .Clock(button_register_2_clock_2),
    .R___W_Selector(button_register_2_r___w_selector_2), .Dataout(button_register_4_dataout),
    .Position___1(button_register_4_position___1), .Address_2(button_register_4_address_2),
    .Driver(button_register_4_driver), .Clock_2(button_register_4_clock_2),
    .R___W_Selector_2(button_register_4_r___w_selector_2), .Zero(button_register_2_zero),
    .Tens(button_register_4_tens), .Units(button_register_4_units));
  // Human_Node human_node_1: pin names not known
  Button_Driver button_driver_2 (
    .Position(button_register_4_driver), .Address_2(button_driver_2_address_2),
    .Address(button_driver_3_address_2), .Button(button_2_out), .Trigger(button_driver_1_trigger));
  Button button_1 (.out(button_1_out));
  // Probe on r1
  // Probe on r2
  // Computer_Node computer_node_3: pin names not known
  Hex_Digit_Display hex_digit_display_7 (.value(button_register_5_units));  // open: dp
  Hex_Digit_Display hex_digit_display_8 (.value(button_register_5_tens));  // open: dp
  LED led_7 (.in(Machine_thinks));
  LED led_8 (.in(Machine_thinks));
  Hex_Digit_Display hex_digit_display_9 (.value(button_register_4_units));  // open: dp
  Hex_Digit_Display hex_digit_display_10 (.value(button_register_4_tens));  // open: dp
  // Human_Node human_node_2: pin names not known
  Button button_2 (.out(button_2_out));
  // Computer_Node computer_node_4: pin names not known
  Button_Register button_register_5 (
    .Data(button_register_7_dataout), .Position(button_register_7_position___1),
    .Address(button_register_7_address_2), .Clock(button_register_7_clock_2),
    .R___W_Selector(button_register_7_r___w_selector_2), .Dataout(button_register_5_dataout),
    .Position___1(button_register_5_position___1), .Address_2(button_register_5_address_2),
    .Clock_2(button_register_5_clock_2), .R___W_Selector_2(button_register_5_r___w_selector_2),
    .Zero(button_register_3_zero), .Tens(button_register_5_tens), .Units(button_register_5_units));  // open: Driver
  Hex_Digit_Display hex_digit_display_11 (.value(button_register_7_tens));  // open: dp
  LED led_9 (.in(Machine_thinks));
  LED led_10 (.in(Game_starts));
  Hex_Digit_Display hex_digit_display_12 (.value(button_register_6_tens));  // open: dp
  Button_Register button_register_6 (
    .Data(button_register_4_dataout), .Position(button_register_4_position___1),
    .Address(button_register_4_address_2), .Clock(button_register_4_clock_2),
    .R___W_Selector(button_register_4_r___w_selector_2), .Dataout(button_register_6_dataout),
    .Position___1(button_register_6_position___1), .Address_2(button_register_6_address_2),
    .Driver(button_register_6_driver), .Clock_2(button_register_6_clock_2),
    .R___W_Selector_2(button_register_6_r___w_selector_2), .Zero(button_register_2_zero),
    .Tens(button_register_6_tens), .Units(button_register_6_units));
  // Human_Node human_node_3: pin names not known
  Button_Driver button_driver_3 (
    .Position(button_register_6_driver), .Address_2(button_driver_3_address_2),
    .Address(button_driver_4_address_2), .Button(button_3_out), .Trigger(button_driver_1_trigger));
  Button button_3 (.out(button_3_out));
  // Probe on r3
  // Probe on r4
  Button_Register button_register_7 (
    .Data(button_register_9_dataout), .Position(button_register_9_position___1),
    .Address(button_register_9_address_2), .Clock(button_register_9_clock_2),
    .R___W_Selector(button_register_9_r___w_selector_2), .Dataout(button_register_7_dataout),
    .Position___1(button_register_7_position___1), .Address_2(button_register_7_address_2),
    .Clock_2(button_register_7_clock_2), .R___W_Selector_2(button_register_7_r___w_selector_2),
    .Zero(button_register_3_zero), .Tens(button_register_7_tens), .Units(button_register_7_units));  // open: Driver
  Hex_Digit_Display hex_digit_display_13 (.value(button_register_7_units));  // open: dp
  LED led_11 (.in(Game_starts));
  LED led_12 (.in(Game_starts));
  Hex_Digit_Display hex_digit_display_14 (.value(button_register_6_units));  // open: dp
  Button_Register button_register_8 (
    .Data(button_register_6_dataout), .Position(button_register_6_position___1),
    .Address(button_register_6_address_2), .Clock(button_register_6_clock_2),
    .R___W_Selector(button_register_6_r___w_selector_2), .Dataout(button_register_8_dataout),
    .Position___1(button_register_8_position___1), .Address_2(button_register_8_address_2),
    .Driver(button_register_8_driver), .Clock_2(button_register_8_clock_2),
    .R___W_Selector_2(button_register_8_r___w_selector_2), .Zero(button_register_2_zero),
    .Tens(button_register_8_tens), .Units(button_register_8_units));
  Button_Driver button_driver_4 (
    .Position(button_register_8_driver), .Address_2(button_driver_4_address_2),
    .Address(button_driver_5_address_2), .Button(button_4_out), .Trigger(button_driver_1_trigger));
  // Probe on PC
  // Probe on SP
  // Computer_Node computer_node_5: pin names not known
  Hex_Digit_Display hex_digit_display_15 (.value(button_register_9_units));  // open: dp
  Hex_Digit_Display hex_digit_display_16 (.value(button_register_9_tens));  // open: dp
  LED led_13 (.in(Checking_rules));
  LED led_14 (.in(Checking_rules));
  LED led_15 (.in(Checking_rules));
  Hex_Digit_Display hex_digit_display_17 (.value(button_register_8_tens));  // open: dp
  Hex_Digit_Display hex_digit_display_18 (.value(button_register_8_units));  // open: dp
  // Human_Node human_node_4: pin names not known
  Button button_4 (.out(button_4_out));
  // Computer_Node computer_node_6: pin names not known
  Button_Register button_register_9 (
    .Data(button_register_11_dataout), .Position(button_register_11_position___1),
    .Address(button_register_11_address_2), .Clock(button_register_11_clock_2),
    .R___W_Selector(button_register_11_r___w_selector_2), .Dataout(button_register_9_dataout),
    .Position___1(button_register_9_position___1), .Address_2(button_register_9_address_2),
    .Clock_2(button_register_9_clock_2), .R___W_Selector_2(button_register_9_r___w_selector_2),
    .Zero(button_register_3_zero), .Tens(button_register_9_tens), .Units(button_register_9_units));  // open: Driver
  Hex_Digit_Display hex_digit_display_19 (.value(button_register_11_tens));  // open: dp
  Hex_Digit_Display hex_digit_display_20 (.value(button_register_11_units));  // open: dp
  LED led_16 (.in(Awaiting_user));
  LED led_17 (.in(Awaiting_user));
  LED led_18 (.in(Awaiting_user));
  Hex_Digit_Display hex_digit_display_21 (.value(button_register_10_tens));  // open: dp
  Hex_Digit_Display hex_digit_display_22 (.value(button_register_10_units));  // open: dp
  Button_Register button_register_10 (
    .Data(button_register_8_dataout), .Position(button_register_8_position___1),
    .Address(button_register_8_address_2), .Clock(button_register_8_clock_2),
    .R___W_Selector(button_register_8_r___w_selector_2), .Dataout(button_register_10_dataout),
    .Position___1(button_register_10_position___1), .Address_2(button_register_10_address_2),
    .Driver(button_register_10_driver), .Clock_2(button_register_10_clock_2),
    .R___W_Selector_2(button_register_10_r___w_selector_2), .Zero(button_register_2_zero),
    .Tens(button_register_10_tens), .Units(button_register_10_units));
  // Human_Node human_node_5: pin names not known
  Button_Driver button_driver_5 (
    .Position(button_register_10_driver), .Address_2(button_driver_5_address_2),
    .Address(button_driver_6_address_2), .Button(button_5_out), .Trigger(button_driver_1_trigger));
  Button button_5 (.out(button_5_out));
  // Probe on PS
  // Computer_Node computer_node_7: pin names not known
  Button_Register button_register_11 (
    .Data(button_register_13_dataout), .Position(button_register_13_position___1),
    .Address(button_register_13_address_2), .Clock(button_register_13_clock_2),
    .R___W_Selector(button_register_13_r___w_selector_2), .Dataout(button_register_11_dataout),
    .Position___1(button_register_11_position___1), .Address_2(button_register_11_address_2),
    .Clock_2(button_register_11_clock_2), .R___W_Selector_2(button_register_11_r___w_selector_2),
    .Zero(button_register_3_zero), .Tens(button_register_11_tens), .Units(button_register_11_units));  // open: Driver
  Hex_Digit_Display hex_digit_display_23 (.value(button_register_13_tens));  // open: dp
  LED led_19 (.in(Calculating_user));
  LED led_20 (.in(Calculating_user));
  Hex_Digit_Display hex_digit_display_24 (.value(button_register_12_tens));  // open: dp
  Button_Register button_register_12 (
    .Data(button_register_10_dataout), .Position(button_register_10_position___1),
    .Address(button_register_10_address_2), .Clock(button_register_10_clock_2),
    .R___W_Selector(button_register_10_r___w_selector_2), .Dataout(button_register_12_dataout),
    .Position___1(button_register_12_position___1), .Address_2(button_register_12_address_2),
    .Driver(button_register_12_driver), .Clock_2(button_register_12_clock_2),
    .R___W_Selector_2(button_register_12_r___w_selector_2), .Zero(button_register_2_zero),
    .Tens(button_register_12_tens), .Units(button_register_12_units));
  Button_Driver button_driver_6 (
    .Position(button_register_12_driver), .Address_2(button_driver_6_address_2), .Button(button_6_out),
    .Trigger(button_driver_1_trigger));  // open: Address
  Button button_6 (.out(button_6_out));
  Button_Register button_register_13 (
    .Data(button_register_14_dataout), .Position(increment_4_bits_1_out_2),
    .Address(button_register_14_address_2), .Clock(button_register_14_clock_2),
    .R___W_Selector(button_register_14_r___w_selector_2), .Dataout(button_register_13_dataout),
    .Position___1(button_register_13_position___1), .Address_2(button_register_13_address_2),
    .Clock_2(button_register_13_clock_2), .R___W_Selector_2(button_register_13_r___w_selector_2),
    .Zero(button_register_3_zero), .Tens(button_register_13_tens), .Units(button_register_13_units));  // open: Driver
  Pull_Resistor #(.pull(1)) pull_resistor_2 (.node(button_register_3_zero));
  Hex_Digit_Display hex_digit_display_25 (.value(button_register_13_units));  // open: dp
  LED led_21 (.in(Calculating_user));
  Win_Lose_Draw win_lose_draw_2 (
    .Tens(button_register_14_tens), .Units(button_register_14_units), .Is_Zero(button_register_2_zero),
    .Another(L), .out_5(H), .out_6(R));
  Pull_Resistor #(.pull(1)) pull_resistor_3 (.node(button_register_2_zero));
  Hex_Digit_Display hex_digit_display_26 (.value(button_register_12_units));  // open: dp
  // Human_Node human_node_6: pin names not known
  Pull_Resistor #(.pull(1)) pull_resistor_4 (.node(button_driver_1_trigger));
  Hex_Digit_Display hex_digit_display_27 (.value(button_register_14_tens));  // open: dp
  Button_Register button_register_14 (
    .Data(button_register_12_dataout), .Position(button_register_12_position___1),
    .Address(button_register_12_address_2), .Clock(button_register_12_clock_2),
    .R___W_Selector(button_register_12_r___w_selector_2), .Dataout(button_register_14_dataout),
    .Position___1(button_register_14_position___1), .Address_2(button_register_14_address_2),
    .Clock_2(button_register_14_clock_2), .R___W_Selector_2(button_register_14_r___w_selector_2),
    .Tens(button_register_14_tens), .Units(button_register_14_units));  // open: Driver, Zero
  Hex_Digit_Display hex_digit_display_28 (.value(button_register_14_units));  // open: dp
  // Human_Node human_node_7: pin names not known
  Increment__4_bits increment_4_bits_1 (.in_1(button_register_14_position___1), .out_2(increment_4_bits_1_out_2));
  LED led_22 (.in(H));
  LED led_23 (.in(H));
  LED led_24 (.in(H));
  Pull_Resistor pull_resistor_5 (.node(H));

  // Notes on the sheet:
  //   Initialization
  //   RAM
  //   contents of rom_1 (hex, n*v repeats v):
  //   d0 f0 d2 0 d3 0 a1 cd f0 d2 4 d3 0 d0 f1 d1 f7 74 ed 18 a2 8c ee 11 a3 d0 f9 d1 ff 74 ed 24 a2 8c ee
  //   1d a3 d1 2 ee
  //   Referee
  //   contents of rom_2 (hex, n*v repeats v):
  //   d0 f0 d2 0 d3 0 a1 d0 e2 b2 d1 f7 79 e0 51 d1 ff 79 e0 51 d1 1 b8 74 e1 51 d0 e1 d1 e2 b2 b7 6b 9b
  //   9b 9b e1 51 b4 3 d2 ff 3b d2 f0 1b be a e1 34 ee 51 d2 e2 b2 d1 0 a1 c b1 8d d2 0 a2 d3 e0 bc d2 2
  //   72 e1 4c d2 f7 ee 4e d2 ff b8 14 a8 d2 0 d0 f9 d1 ff d6 9c d0 f1 d1 f7 d6 9c a e1 63 d4 d2 0 d0 f1
  //   d6 9c a e1 70 d1 3 ee 0 d2 e2 b9 71 e1 7a d1 2 ee 0 d0 f9 d1 ff d2 0 d6 9c a e1 89 d1 2 ee 0 d2 e2
  //   b9 71 e1 93 d1 3 ee 0 d1 5 d3 e0 bc 34 1 ee 0 71 e0 a4 b3 1e 8c ee 9c d7
  //   User
  //   contents of rom_3 (hex, n*v repeats v):
  //   d0 f0 d2 0 d3 0 a1 d0 f8 d1 ff d2 ff a1 b1 76 e0 e d2 f0 a2 d3 e1 ad b4 d2 0 a6 0 ed 33 8d d2 f8 76
  //   e1 26 8d d2 ff 76 e1 2d d1 f1 b7 8f a7 88 ee 1c d3 e2 ad d3 e0 d2 2 ae d1 1 ee
  //   User Input Register
  //   Computer
  //   contents of rom_4 (hex, n*v repeats v):
  //   d0 f0 d2 0 d3 0 a1 d0 f8 d1 ff a1 d0 f9 d2 d d3 ff 73 ea 28 b1 76 eb 1f 36 9 d2 d ee 16 11 77 e1 25
  //   ee 52 8c ee 12 d0 f9 d3 ff 73 ea 41 b1 76 e0 3c 11 b7 f e1 3e b1 5 ed 3e ee 52 8c ee 2a d0 ff 88 d1
  //   f9 71 eb 52 b2 a ed 4f ee 52 88 ee 46 d3 e1 ac 1 d0 f8 d2 f0 a2 b4 d2 0 a6 0 ed 77 d2 ff 76 e1 69 d1
  //   f0 8d d2 f7 76 e1 71 d1 f9 b7 8f a7 88 ee 5f d3 e2 ad d3 e0 d2 3 ae d1 1 ee
endmodule
